// Logisim project FatmaEremAKsoy_2315075_ALU8.circ as structural Verilog
module FULLADDER (
  input  X,
  input  Y,
  input  CIN,
  output SUM,
  output COUT
);

  wire and_1_out, and_2_out, xor_1_out;

  xor xor_1 (xor_1_out, X, Y);
  xor xor_2 (SUM, xor_1_out, CIN);
  and and_1 (and_1_out, xor_1_out, CIN);
  and and_2 (and_2_out, Y, X);
  or or_1 (COUT, and_1_out, and_2_out);
endmodule

module FULLADDER8 (
  input  CIN,
  input  [7:0] X,
  input  [7:0] Y,
  output [7:0] SUM,
  output COUT
);

  wire fulladder_1_cout, fulladder_2_cout, fulladder_3_cout, fulladder_4_cout, fulladder_5_cout,
       fulladder_6_cout, fulladder_7_cout;

  FULLADDER fulladder_1 (.X(X[0]), .Y(Y[0]), .CIN(CIN), .SUM(SUM[0]), .COUT(fulladder_1_cout));
  FULLADDER fulladder_2 (.X(X[1]), .Y(Y[1]), .CIN(fulladder_1_cout), .SUM(SUM[1]), .COUT(fulladder_2_cout));
  FULLADDER fulladder_3 (.X(X[2]), .Y(Y[2]), .CIN(fulladder_2_cout), .SUM(SUM[2]), .COUT(fulladder_3_cout));
  FULLADDER fulladder_4 (.X(X[3]), .Y(Y[3]), .CIN(fulladder_3_cout), .SUM(SUM[3]), .COUT(fulladder_4_cout));
  FULLADDER fulladder_5 (.X(X[4]), .Y(Y[4]), .CIN(fulladder_4_cout), .SUM(SUM[4]), .COUT(fulladder_5_cout));
  FULLADDER fulladder_6 (.X(X[5]), .Y(Y[5]), .CIN(fulladder_5_cout), .SUM(SUM[5]), .COUT(fulladder_6_cout));
  FULLADDER fulladder_7 (.X(X[6]), .Y(Y[6]), .CIN(fulladder_6_cout), .SUM(SUM[6]), .COUT(fulladder_7_cout));
  FULLADDER fulladder_8 (.X(X[7]), .Y(Y[7]), .CIN(fulladder_7_cout), .SUM(SUM[7]), .COUT(COUT));
endmodule

module rotl (
  input  [7:0] inputA,
  input  [2:0] inputB,
  output [7:0] O3
);

  Multiplexer #(.select(3), .width(8)) multiplexer_1 (
    .in0(inputA), .in1({inputA[6:0], inputA[7]}), .in2({inputA[5:0], inputA[7:6]}),
    .in3({inputA[4:0], inputA[7:5]}), .in4({inputA[3:0], inputA[7:4]}), .in5({inputA[2:0], inputA[7:3]}),
    .in6({inputA[1:0], inputA[7:2]}), .in7({inputA[0], inputA[7:1]}), .out(O3), .sel(inputB));
endmodule

module ALU8 (
  input  [7:0] X,
  input  [7:0] Y,
  input  [1:0] Opcode,
  output OVF,
  output CF,
  output [7:0] RESULT,
  output EQ,
  output ZF,
  output SF
);

  wire not_2_out, not_3_out, not_4_out, not_5_out, not_6_out, not_7_out, not_8_out, not_9_out;
  wire [7:0] and_1_out, fulladder8_1_sum, or_1_out, rotl_1_o3, xnor_1_out;

  assign and_1_out = X & Y;  // AND_Gate and_1, 8 bits wide
  assign xnor_1_out = ~(X ^ Y);  // XNOR_Gate xnor_1, 8 bits wide
  assign or_1_out = X | Y;  // OR_Gate or_1, 8 bits wide
  FULLADDER8 fulladder8_1 (.CIN(Opcode[0]), .X(X), .Y(Y), .SUM(fulladder8_1_sum), .COUT(OVF));
  and and_2 (EQ, xnor_1_out[0], xnor_1_out[1], xnor_1_out[2], xnor_1_out[3], xnor_1_out[4], xnor_1_out[5], xnor_1_out[6], xnor_1_out[7]);
  rotl rotl_1 (.inputA(X), .inputB(Y[2:0]), .O3(rotl_1_o3));
  not not_1 (CF, OVF);
  Multiplexer #(.select(2), .width(8)) multiplexer_1 (
    .in0(fulladder8_1_sum), .in1(and_1_out), .in2(or_1_out), .in3(rotl_1_o3), .out(RESULT), .sel(Opcode));
  not not_2 (not_2_out, RESULT[0]);
  not not_3 (not_3_out, RESULT[1]);
  not not_4 (not_4_out, RESULT[2]);
  not not_5 (not_5_out, RESULT[3]);
  not not_6 (not_6_out, RESULT[4]);
  not not_7 (not_7_out, RESULT[5]);
  not not_8 (not_8_out, RESULT[6]);
  not not_9 (not_9_out, RESULT[7]);
  and and_3 (ZF, not_2_out, not_3_out, not_4_out, not_5_out, not_6_out, not_7_out, not_8_out, not_9_out);

  assign SF = RESULT[7];
endmodule
