// Logisim project FatmaEremAksoy_2315075_FADDER8.circ as structural Verilog
module FULLADDER (
  input  X,
  input  Y,
  input  CIN,
  output SUM,
  output COUT
);

  wire and_1_out, and_2_out, xor_1_out;

  xor xor_1 (xor_1_out, X, Y);
  xor xor_2 (SUM, xor_1_out, CIN);
  and and_1 (and_1_out, xor_1_out, CIN);
  and and_2 (and_2_out, Y, X);
  or or_1 (COUT, and_1_out, and_2_out);
endmodule

module FULLADDER8 (
  input  CIN,
  input  [7:0] X,
  input  [7:0] Y,
  output [7:0] SUM,
  output COUT
);

  wire fulladder_1_cout, fulladder_2_cout, fulladder_3_cout, fulladder_4_cout, fulladder_5_cout,
       fulladder_6_cout, fulladder_7_cout;

  FULLADDER fulladder_1 (.X(X[0]), .Y(Y[0]), .CIN(CIN), .SUM(SUM[0]), .COUT(fulladder_1_cout));
  FULLADDER fulladder_2 (.X(X[1]), .Y(Y[1]), .CIN(fulladder_1_cout), .SUM(SUM[1]), .COUT(fulladder_2_cout));
  FULLADDER fulladder_3 (.X(X[2]), .Y(Y[2]), .CIN(fulladder_2_cout), .SUM(SUM[2]), .COUT(fulladder_3_cout));
  FULLADDER fulladder_4 (.X(X[3]), .Y(Y[3]), .CIN(fulladder_3_cout), .SUM(SUM[3]), .COUT(fulladder_4_cout));
  FULLADDER fulladder_5 (.X(X[4]), .Y(Y[4]), .CIN(fulladder_4_cout), .SUM(SUM[4]), .COUT(fulladder_5_cout));
  FULLADDER fulladder_6 (.X(X[5]), .Y(Y[5]), .CIN(fulladder_5_cout), .SUM(SUM[5]), .COUT(fulladder_6_cout));
  FULLADDER fulladder_7 (.X(X[6]), .Y(Y[6]), .CIN(fulladder_6_cout), .SUM(SUM[6]), .COUT(fulladder_7_cout));
  FULLADDER fulladder_8 (.X(X[7]), .Y(Y[7]), .CIN(fulladder_7_cout), .SUM(SUM[7]), .COUT(COUT));
endmodule
