// Logisim project TP_Part1.circ as structural Verilog: 4 circuits, main circuit main
module main (
);

  subcircuit1 subcircuit1_1 ();  // open: Input1, O1, O2
endmodule

module subcircuit1 (
  input  [7:0] Input1,
  output O1,
  output [7:0] O2
);

  not not_1 (O2[7], Input1[7]);
  buf and_1 (O1, Input1[0]);  // AND_Gate

  assign O2[6:0] = Input1[6:0];
endmodule

module rotr (
  input  [7:0] inputA,
  input  [2:0] inputB,
  output [7:0] O3
);

  Multiplexer #(.select(3), .width(8)) multiplexer_1 (
    .in0(inputA), .in1({inputA[0], inputA[7:1]}), .in2({inputA[1:0], inputA[7:2]}),
    .in3({inputA[2:0], inputA[7:3]}), .in4({inputA[3:0], inputA[7:4]}), .in5({inputA[4:0], inputA[7:5]}),
    .in6({inputA[5:0], inputA[7:6]}), .in7({inputA[6:0], inputA[7]}), .out(O3), .sel(inputB));
endmodule

module rotl (
  input  [7:0] inputA,
  input  [2:0] inputB,
  output [7:0] O3
);

  Multiplexer #(.select(3), .width(8)) multiplexer_1 (
    .in0(inputA), .in1({inputA[6:0], inputA[7]}), .in2({inputA[5:0], inputA[7:6]}),
    .in3({inputA[4:0], inputA[7:5]}), .in4({inputA[3:0], inputA[7:4]}), .in5({inputA[2:0], inputA[7:3]}),
    .in6({inputA[1:0], inputA[7:2]}), .in7({inputA[0], inputA[7:1]}), .out(O3), .sel(inputB));
endmodule
