// Logisim project TP_Part2.circ as structural Verilog: 7 circuits, main circuit main
module main (
);

  wire control_unit_1_mux2, control_unit_1_mw, control_unit_1_we, control_unit_1_wr;
  wire [1:0] control_unit_1_alufunc, control_unit_1_mux1;
  wire [2:0] instr_mem_1_rd, instr_mem_1_rs, instr_mem_1_rt;
  wire [3:0] instr_mem_1_opcode;
  wire [7:0] alu_8_1_result, data_mem_1_z, instr_mem_1_immediate, multiplexer_1_out, multiplexer_2_out,
       reg_file_1_x, reg_file_1_y;
  wire [9:0] pc_1_pc_out;

  PC pc_1 (.PC_OUT(pc_1_pc_out));
  Instr_Mem instr_mem_1 (
    .ROM_Addr(pc_1_pc_out), .Immediate(instr_mem_1_immediate), .rd(instr_mem_1_rd), .rt(instr_mem_1_rt),
    .rs(instr_mem_1_rs), .opcode(instr_mem_1_opcode));
  Multiplexer #(.select(2), .width(8)) multiplexer_1 (
    .in0(alu_8_1_result), .in1(data_mem_1_z), .in2(instr_mem_1_immediate), .in3({8{1'b0}}),
    .out(multiplexer_1_out), .sel(control_unit_1_mux1));
  Control_Unit control_unit_1 (
    .opcode(instr_mem_1_opcode), .MUX1(control_unit_1_mux1), .MUX2(control_unit_1_mux2),
    .WE(control_unit_1_we), .MW(control_unit_1_mw), .WR(control_unit_1_wr), .ALUfunc(control_unit_1_alufunc));
  Reg_File reg_file_1 (
    .WE(control_unit_1_we), .rd(instr_mem_1_rd), .Instr(multiplexer_1_out), .rs(instr_mem_1_rs),
    .rt(instr_mem_1_rt), .X(reg_file_1_x), .Y(reg_file_1_y));
  Multiplexer #(.width(8)) multiplexer_2 (
    .in0(reg_file_1_y), .out(multiplexer_2_out), .sel(control_unit_1_mux2));  // open: in1
  ALU_8 alu_8_1 (.X(reg_file_1_x), .Y(multiplexer_2_out), .ALUfunc(control_unit_1_alufunc), .RESULT(alu_8_1_result));
  Data_Mem data_mem_1 (
    .X(alu_8_1_result), .WRITE(control_unit_1_mw), .READ(control_unit_1_wr), .Y(reg_file_1_y),
    .Z(data_mem_1_z));
endmodule

module Reg_File (
  input  WE,
  input  [2:0] rd,
  input  [7:0] Instr,
  input  [2:0] rs,
  input  [2:0] rt,
  output [7:0] X,
  output [7:0] Y
);

  wire C_out, decoder_1_out0, decoder_1_out1, decoder_1_out2, decoder_1_out3, decoder_1_out4, decoder_1_out5,
       decoder_1_out6, decoder_1_out7;
  wire [7:0] register_1_q, register_2_q, register_3_q, register_4_q, register_5_q, register_6_q,
       register_7_q, register_8_q;

  Decoder #(.select(3)) decoder_1 (
    .out0(decoder_1_out0), .out1(decoder_1_out1), .out2(decoder_1_out2), .out3(decoder_1_out3),
    .out4(decoder_1_out4), .out5(decoder_1_out5), .out6(decoder_1_out6), .out7(decoder_1_out7), .sel(rd),
    .en(WE));
  Clock C (.out(C_out));
  Multiplexer #(.select(3), .width(8)) multiplexer_1 (
    .in0(register_1_q), .in1(register_2_q), .in2(register_3_q), .in3(register_4_q), .in4(register_5_q),
    .in5(register_6_q), .in6(register_7_q), .in7(register_8_q), .out(X), .sel(rs));
  Multiplexer #(.select(3), .width(8)) multiplexer_2 (
    .in0(register_1_q), .in1(register_2_q), .in2(register_3_q), .in3(register_4_q), .in4(register_5_q),
    .in5(register_6_q), .in6(register_7_q), .in7(register_8_q), .out(Y), .sel(rt));
  Register #(.trigger("falling")) register_1 (
    .D(Instr), .en(decoder_1_out0), .clk(C_out), .Q(register_1_q));  // open: clr
  Register #(.trigger("falling")) register_2 (
    .D(Instr), .en(decoder_1_out1), .clk(C_out), .Q(register_2_q));  // open: clr
  Register #(.trigger("falling")) register_3 (
    .D(Instr), .en(decoder_1_out2), .clk(C_out), .Q(register_3_q));  // open: clr
  Register #(.trigger("falling")) register_4 (
    .D(Instr), .en(decoder_1_out3), .clk(C_out), .Q(register_4_q));  // open: clr
  Register #(.trigger("falling")) register_5 (
    .D(Instr), .en(decoder_1_out4), .clk(C_out), .Q(register_5_q));  // open: clr
  Register #(.trigger("falling")) register_6 (
    .D(Instr), .en(decoder_1_out5), .clk(C_out), .Q(register_6_q));  // open: clr
  Register #(.trigger("falling")) register_7 (
    .D(Instr), .en(decoder_1_out6), .clk(C_out), .Q(register_7_q));  // open: clr
  Register #(.trigger("falling")) register_8 (
    .D(Instr), .en(decoder_1_out7), .clk(C_out), .Q(register_8_q));  // open: clr
endmodule

module Instr_Mem (
  input  [9:0] ROM_Addr,
  output [7:0] Immediate,
  output [2:0] rd,
  output [2:0] rt,
  output [2:0] rs,
  output [3:0] opcode
);

  wire [7:0] rom_1_data;
  wire [16:8] rom_1_data_2;
  wire [20:17] multiplexer_1_out;

  ROM #(.addrWidth(10), .dataWidth(21)) rom_1 (.addr(ROM_Addr), .data({opcode, rom_1_data_2, rom_1_data}));
  Multiplexer #(.select(4), .width(21)) multiplexer_1 (
    .in0({opcode, rom_1_data_2, rom_1_data}), .in1({opcode, rom_1_data_2, rom_1_data}),
    .in2({opcode, rom_1_data_2, rom_1_data}), .in3({opcode, rom_1_data_2, rom_1_data}),
    .in4({opcode, rom_1_data_2, rom_1_data}), .in8({opcode, rom_1_data_2, rom_1_data}),
    .in12({opcode, rom_1_data_2, rom_1_data}), .out({multiplexer_1_out, rs, rt, rd, Immediate}), .sel(opcode));  // open: in5, in6, in7, in9, in10, in11, in13, in14, in15
  // also tied to GND on the sheet: {rom_1_data[0], rom_1_data[1], rom_1_data[2], rom_1_data[3], rom_1_data[4], rom_1_data[5], rom_1_data[6], rom_1_data[7]}

  // Notes on the sheet:
  //   contents of rom_1 (hex, n*v repeats v):
  //   60108 60204 88b00 8c00 188d00 45000 24600
endmodule

module Data_Mem (
  input  [7:0] X,
  input  WRITE,
  input  READ,
  input  [7:0] Y,
  output [7:0] Z
);

  wire C_out;

  Clock C (.out(C_out));
  RAM #(.trigger("falling")) ram_1 (.addr(X), .we(WRITE), .oe(READ), .clk(C_out), .din(Y), .dout(Z));
endmodule

module ALU_8 (
  input  [7:0] X,
  input  [7:0] Y,
  input  [1:0] ALUfunc,
  output [7:0] RESULT
);

  wire [7:0] adder_1_out, and_1_out, or_1_out, shifter_1_out;

  Adder adder_1 (.a(X), .b(Y), .out(adder_1_out));  // open: cin, cout
  Shifter #(.shift("rl")) shifter_1 (.in(X), .\dist (Y[2:0]), .out(shifter_1_out));
  assign and_1_out = X & Y;  // AND_Gate and_1, 8 bits wide
  assign or_1_out = X | Y;  // OR_Gate or_1, 8 bits wide
  Multiplexer #(.select(2), .width(8)) multiplexer_1 (
    .in0(adder_1_out), .in1(and_1_out), .in2(or_1_out), .in3(shifter_1_out), .out(RESULT), .sel(ALUfunc));
endmodule

module Control_Unit (
  input  [3:0] opcode,
  output [1:0] MUX1,
  output MUX2,
  output WE,
  output MW,
  output WR,
  output [1:0] ALUfunc
);

  wire not_1_out, not_2_out, not_3_out, not_4_out;

  not not_1 (not_1_out, opcode[1]);
  not not_2 (not_2_out, opcode[1]);
  not not_3 (not_3_out, opcode[0]);
  and and_1 (MUX1[1], opcode[0], opcode[1]);
  and and_2 (MUX1[0], opcode[0], not_1_out);
  or or_1 (MUX2, opcode[0], opcode[1]);
  or or_2 (WE, not_2_out, opcode[0]);
  and and_3 (MW, opcode[1], not_3_out);
  not not_4 (not_4_out, opcode[1]);
  and and_4 (WR, not_4_out, opcode[0]);

  assign ALUfunc = opcode[3:2];
endmodule

module PC (
  output [9:0] PC_OUT
);

  wire C_out;
  wire [9:0] adder_1_out;

  Clock C (.out(C_out));
  Counter #(.max('h3ff), .ongoal("continue"), .trigger("falling"), .width(10)) counter_1 (
    .D(adder_1_out), .Q(PC_OUT), .clk(C_out));  // open: load, count, carry, up, clr
  Adder #(.width(10)) adder_1 (.a(PC_OUT), .b(10'h1), .out(adder_1_out));  // open: cin, cout
endmodule
