// Logisim project TP_Part3.circ as structural Verilog: 7 circuits, main circuit main
module main (
);

  wire alu_8_1_eq, bit_extender_2_out, clk_out, control_unit_1_mux2, control_unit_1_read, control_unit_1_we,
       control_unit_1_write;
  wire [1:0] and_1_out, control_unit_1_mux1, control_unit_1_pcmux, undriven;
  wire [2:0] control_unit_1_alufunc, instr_mem_1_rd, instr_mem_1_rs, instr_mem_1_rt;
  wire [3:0] instr_mem_1_opcode;
  wire [7:0] alu_8_1_result, bit_extender_1_out, data_mem_1_z, multiplexer_2_out, multiplexer_3_out,
       reg_file_1_x, reg_file_1_y;
  wire [9:0] adder_1_out, adder_2_out, instr_mem_1_jmp_imm, multiplexer_1_out, pc_1_pc_out, undriven_2;

  Clock clk (.out(clk_out));
  Multiplexer #(.select(2), .width(10)) multiplexer_1 (
    .in0(adder_1_out), .in1(adder_2_out), .in2(instr_mem_1_jmp_imm), .in3({10{1'b0}}),
    .out(multiplexer_1_out), .sel(and_1_out));
  assign and_1_out = control_unit_1_pcmux & undriven;  // AND_Gate and_1, 2 bits wide
  PC pc_1 (.PC_IN(multiplexer_1_out), .clk(clk_out), .PC_OUT(pc_1_pc_out));
  Adder #(.width(10)) adder_1 (.a(pc_1_pc_out), .b(10'h1), .out(adder_1_out));  // open: cin, cout
  Adder #(.width(10)) adder_2 (.a(pc_1_pc_out), .b(undriven_2), .out(adder_2_out));  // open: cin, cout
  Bit_Extender #(.in_width(10), .out_width(8)) bit_extender_1 (.in(undriven_2), .out(bit_extender_1_out));
  Bit_Extender #(.in_width(2), .out_width(1)) bit_extender_2 (.in(undriven), .out(bit_extender_2_out));
  Instr_Mem instr_mem_1 (
    .ROM_Addr(pc_1_pc_out), .IMM(bit_extender_1_out), .rd(instr_mem_1_rd), .rt(instr_mem_1_rt),
    .rs(instr_mem_1_rs), .opcode(instr_mem_1_opcode), .JMP_IMM(instr_mem_1_jmp_imm));
  Control_Unit control_unit_1 (
    .Opcode(instr_mem_1_opcode), .EQ(alu_8_1_eq), .ALUfunc(control_unit_1_alufunc),
    .Mux1(control_unit_1_mux1), .Mux2(control_unit_1_mux2), .WE(control_unit_1_we),
    .WRITE(control_unit_1_write), .READ(control_unit_1_read), .PCMux(control_unit_1_pcmux),
    .Branch(bit_extender_2_out));
  Multiplexer #(.select(2), .width(8)) multiplexer_2 (
    .in0(alu_8_1_result), .in1(data_mem_1_z), .in2(bit_extender_1_out), .out(multiplexer_2_out),
    .sel(control_unit_1_mux1));  // open: in3
  Reg_File reg_file_1 (
    .WE(control_unit_1_we), .rd(instr_mem_1_rd), .Instr(multiplexer_2_out), .clk(clk_out),
    .rs(instr_mem_1_rt), .rt(instr_mem_1_rs), .X(reg_file_1_x), .Y(reg_file_1_y));
  Multiplexer #(.width(8)) multiplexer_3 (
    .in0(reg_file_1_y), .in1(bit_extender_1_out), .out(multiplexer_3_out), .sel(control_unit_1_mux2));
  ALU_8 alu_8_1 (
    .X(reg_file_1_x), .Y(multiplexer_3_out), .ALUfunc(control_unit_1_alufunc), .RESULT(alu_8_1_result),
    .EQ(alu_8_1_eq));
  Data_Mem data_mem_1 (
    .X(alu_8_1_result), .WRITE(control_unit_1_write), .READ(control_unit_1_read), .clk(clk_out),
    .Y(reg_file_1_y), .Z(data_mem_1_z));
endmodule

module ALU_8 (
  input  [7:0] X,
  input  [7:0] Y,
  input  [2:0] ALUfunc,
  output [7:0] RESULT,
  output EQ
);

  wire comparator_1_lt;
  wire [7:0] adder_1_out, and_1_out, bit_extender_1_out, or_1_out, shifter_1_out;

  Adder adder_1 (.a(X), .b(Y), .out(adder_1_out));  // open: cin, cout
  Shifter #(.shift("rl")) shifter_1 (.in(X), .\dist (Y[2:0]), .out(shifter_1_out));
  Comparator comparator_1 (.a(X), .b(Y), .eq(EQ), .lt(comparator_1_lt));  // open: gt
  assign and_1_out = X & Y;  // AND_Gate and_1, 8 bits wide
  assign or_1_out = X | Y;  // OR_Gate or_1, 8 bits wide
  assign bit_extender_1_out = {{7{comparator_1_lt}}, comparator_1_lt};  // Bit_Extender bit_extender_1
  Multiplexer #(.select(3), .width(8)) multiplexer_1 (
    .in0(adder_1_out), .in1(and_1_out), .in2(or_1_out), .in3(shifter_1_out), .in4(bit_extender_1_out),
    .out(RESULT), .sel(ALUfunc));  // open: in5, in6, in7
endmodule

module Control_Unit (
  input  [3:0] Opcode,
  input  EQ,
  output [2:0] ALUfunc,
  output [1:0] Mux1,
  output Mux2,
  output WE,
  output WRITE,
  output READ,
  output [1:0] PCMux,
  output Branch
);

  wire and_6_out, and_7_out, and_8_out, and_9_out, and_10_out, and_15_out, and_16_out, and_17_out, not_1_out,
       not_2_out, not_3_out, not_4_out, not_5_out;

  not not_1 (not_1_out, Opcode[3]);
  not not_2 (not_2_out, Opcode[2]);
  not not_3 (not_3_out, Opcode[1]);
  not not_4 (not_4_out, Opcode[0]);
  not not_5 (not_5_out, EQ);
  and and_1 (ALUfunc[2], Opcode[3], Opcode[0]);
  and and_2 (ALUfunc[1], Opcode[3], not_3_out);
  and and_3 (ALUfunc[0], Opcode[2], not_3_out);
  and and_4 (Mux1[1], not_2_out, Opcode[1]);
  and and_5 (Mux1[0], not_3_out, Opcode[0]);
  and and_6 (and_6_out, not_2_out, Opcode[0]);
  and and_7 (and_7_out, not_2_out, Opcode[1]);
  and and_8 (and_8_out, not_1_out, not_2_out, Opcode[0]);
  and and_9 (and_9_out, not_3_out, not_4_out);
  and and_10 (and_10_out, Opcode[3], Opcode[2]);
  and and_11 (WRITE, Opcode[1], not_4_out);
  and and_12 (READ, not_2_out, not_3_out, Opcode[0]);
  and and_13 (PCMux[1], Opcode[3], not_2_out, Opcode[0]);
  and and_14 (PCMux[0], not_1_out, Opcode[2], Opcode[0]);
  and and_15 (and_15_out, Opcode[3], not_2_out, Opcode[0]);
  and and_16 (and_16_out, Opcode[2], not_3_out, Opcode[0], EQ);
  and and_17 (and_17_out, not_1_out, Opcode[2], Opcode[1], not_5_out);
  or or_1 (Mux2, and_6_out, and_7_out);
  or or_2 (WE, and_8_out, and_9_out, and_10_out);
  or or_3 (Branch, and_15_out, and_16_out, and_17_out);
endmodule

module Reg_File (
  input  WE,
  input  [2:0] rd,
  input  [7:0] Instr,
  input  clk,
  input  [2:0] rs,
  input  [2:0] rt,
  output [7:0] X,
  output [7:0] Y
);

  wire decoder_1_out0, decoder_1_out1, decoder_1_out2, decoder_1_out3, decoder_1_out4, decoder_1_out5,
       decoder_1_out6, decoder_1_out7;
  wire [7:0] register_1_q, register_2_q, register_3_q, register_4_q, register_5_q, register_6_q,
       register_7_q, register_8_q;

  Decoder #(.select(3)) decoder_1 (
    .out0(decoder_1_out0), .out1(decoder_1_out1), .out2(decoder_1_out2), .out3(decoder_1_out3),
    .out4(decoder_1_out4), .out5(decoder_1_out5), .out6(decoder_1_out6), .out7(decoder_1_out7), .sel(rd),
    .en(WE));
  Multiplexer #(.select(3), .width(8)) multiplexer_1 (
    .in0(register_1_q), .in1(register_2_q), .in2(register_3_q), .in3(register_4_q), .in4(register_5_q),
    .in5(register_6_q), .in6(register_7_q), .in7(register_8_q), .out(X), .sel(rs));
  Multiplexer #(.select(3), .width(8)) multiplexer_2 (
    .in0(register_1_q), .in1(register_2_q), .in2(register_3_q), .in3(register_4_q), .in4(register_5_q),
    .in5(register_6_q), .in6(register_7_q), .in7(register_8_q), .out(Y), .sel(rt));
  Register #(.trigger("falling")) register_1 (
    .D(Instr), .en(decoder_1_out0), .clk(clk), .Q(register_1_q));  // open: clr
  Register #(.trigger("falling")) register_2 (
    .D(Instr), .en(decoder_1_out1), .clk(clk), .Q(register_2_q));  // open: clr
  Register #(.trigger("falling")) register_3 (
    .D(Instr), .en(decoder_1_out2), .clk(clk), .Q(register_3_q));  // open: clr
  Register #(.trigger("falling")) register_4 (
    .D(Instr), .en(decoder_1_out3), .clk(clk), .Q(register_4_q));  // open: clr
  Register #(.trigger("falling")) register_5 (
    .D(Instr), .en(decoder_1_out4), .clk(clk), .Q(register_5_q));  // open: clr
  Register #(.trigger("falling")) register_6 (
    .D(Instr), .en(decoder_1_out5), .clk(clk), .Q(register_6_q));  // open: clr
  Register #(.trigger("falling")) register_7 (
    .D(Instr), .en(decoder_1_out6), .clk(clk), .Q(register_7_q));  // open: clr
  Register #(.trigger("falling")) register_8 (
    .D(Instr), .en(decoder_1_out7), .clk(clk), .Q(register_8_q));  // open: clr
endmodule

module Instr_Mem (
  input  [9:0] ROM_Addr,
  output [7:0] IMM,
  output [2:0] rd,
  output [2:0] rt,
  output [2:0] rs,
  output [3:0] opcode,
  output [9:0] JMP_IMM
);

  ROM #(.addrWidth(10), .dataWidth(21)) rom_1 (.addr(ROM_Addr), .data({opcode, rs, rt, rd[2], JMP_IMM[9:8], IMM}));

  assign JMP_IMM[7:0] = IMM;
  assign rd[1:0] = JMP_IMM[9:8];

  // Notes on the sheet:
  //   contents of rom_1 (hex, n*v repeats v):
  //   60306 60601 6040c 1f700 1f3d00 bf0fe 160009 b200
endmodule

module Data_Mem (
  input  [7:0] X,
  input  WRITE,
  input  READ,
  input  clk,
  input  [7:0] Y,
  output [7:0] Z
);

  RAM #(.trigger("falling")) ram_1 (.addr(X), .we(WRITE), .oe(READ), .clk(clk), .din(Y), .dout(Z));
endmodule

module PC (
  input  [9:0] PC_IN,
  input  clk,
  output [9:0] PC_OUT
);

  Counter #(.max('h3ff), .ongoal("continue"), .trigger("falling"), .width(10)) counter_1 (
    .D(PC_IN), .Q(PC_OUT), .clk(clk));  // open: load, count, carry, up, clr
endmodule
